# Fritzing sketch MiniCat_2.0_PCB_1_0 (saved by Fritzing 0.9.4)
circuit board: 8.02503cm x 5.41867cm
breadboards: 1

parts:
  IR = female pin header, 3 pins [form="♀ (female)"]
  buzzer = female pin header, 2 pins [form="♀ (female)"]
  mpu_6051 = InvenSense MPU6050
  arduino_nano1 = Arduino Nano (Rev3.0)
  J1 = female pin header, 6 pins [form="♀ (female)"]
  J2 = female pin header, 6 pins [form="♀ (female)"]

nets:
  N1: IR.pin1, buzzer.pin1, J2.pin1
  N2: IR.pin2, arduino_nano1.5V, J2.pin5
  N3: IR.pin3, arduino_nano1.D5
  N4: buzzer.pin2, arduino_nano1.D4
  N5: mpu_6051.VCC, J1.pin5
  GND: mpu_6051.GND, arduino_nano1.GND, J1.pin1
  N6: mpu_6051.SCL, J1.pin3
  N7: mpu_6051.SDA, J1.pin4
  N8: mpu_6051.INT, arduino_nano1.D2
  N9: arduino_nano1.VIN, J1.pin6
  N10: arduino_nano1.A5, J2.pin3
  N11: arduino_nano1.A4, J2.pin4

notes:
  ->
  to batt
  roboticsformakers.com
  (usb side)
  (GND)
  -
  +
  S
