# Fritzing sketch MiniCat_2.0_PCB_1x_LAYER_1_0 (saved by Fritzing 0.9.4)
circuit board: 8.02503cm x 5.41867cm
breadboards: 1

parts:
  IR = female pin header, 3 pins [form="♀ (female)"]
  buzzer = female pin header, 2 pins [form="♀ (female)"]
  mpu_6051 = InvenSense MPU6050
  J1 = female pin header, 6 pins [form="♀ (female)"]
  J2 = female pin header, 6 pins [form="♀ (female)"]
  arduino_nano1 = Arduino Nano (Rev3.0)

nets:
  N1: IR.pin1, buzzer.pin1, J2.pin1
  VCC: IR.pin2, mpu_6051.VCC, J2.pin5, arduino_nano1.5V
  N2: IR.pin3, arduino_nano1.D5
  N3: buzzer.pin2, arduino_nano1.D4
  GND: mpu_6051.GND, J1.pin1, arduino_nano1.GND
  N4: mpu_6051.SCL, J1.pin3
  N5: mpu_6051.SDA, J1.pin4
  N6: mpu_6051.INT, arduino_nano1.D2
  N7: J1.pin6, arduino_nano1.VIN
  N8: J2.pin3, arduino_nano1.A5
  N9: J2.pin4, arduino_nano1.A4

notes:
  ->
  to batt
  roboticsformakers.com
  (usb side)
  (GND)
  -
  +
  S
