# Fritzing sketch MiniCat_Buzzer_Infrared_Servo_IMU_EYES__FULL__Sketch (saved by Fritzing 0.9.4)

parts:
  Part1 = Arduino Nano (Rev3.0) (ICSP)
  Part2 = 16-Channel 12-bit PWM Servo Driver - I2C [part_number=815]
  Part3 = InvenSense MPU6050
  IR1 = TSOP312.., 314.. [package=THT]
  J1 = Basic Servo
  J2 = Piezo Speaker
  J3 = Basic Servo
  J4 = Basic Servo
  J5 = Basic Servo
  J6 = Basic Servo
  J7 = Basic Servo
  J8 = Basic Servo
  J9 = Basic Servo
  VCC1 = Battery
  Part4 = Arduino Nano (Rev3.0) (ICSP)
  OLED_I2C1 = OLED 128x64 I2C Monochrome Display  # not connected
  OLED_I2C2 = OLED 128x64 I2C Monochrome Display

nets:
  GND: Part1.GND, Part2.GND, Part3.GND, J1.gnd, J3.gnd, J4.gnd, J5.gnd, J6.gnd, J7.gnd, J8.gnd, J9.gnd, VCC1.-
  N1: Part1.D2, Part3.INT
  N2: Part1.D4, J2.pin2
  N3: Part1.D5, IR1.Data, Part4.D5
  VCC: Part1.VIN, Part2.5.0V, J1.vcc, J3.vcc, J4.vcc, J5.vcc, J6.vcc, J7.vcc, J8.vcc, J9.vcc
  VCC_2: Part1.5V, Part2.VCC, Part3.VCC
  N4: Part1.A5, Part2.SCL, Part3.SCL
  N5: Part1.A4, Part2.SDA, Part3.SDA
  N6: Part2.PWRIN, VCC1.+
  N7: Part2.PWM7, J5.pulse
  N8: Part2.PWM6, J4.pulse
  N9: Part2.PWM5, J3.pulse
  N10: Part2.PWM4, J1.pulse
  N11: Part2.PWM11, J6.pulse
  N12: Part2.PWM10, J9.pulse
  N13: Part2.PWM9, J7.pulse
  N14: Part2.PWM8, J8.pulse
  GND_2: J2.pin1, Part4.GND, OLED_I2C2.GND
  5V: Part4.5V, OLED_I2C2.VDD
  N15: Part4.A5, OLED_I2C2.SCK
  N16: Part4.A4, OLED_I2C2.SDA

custom parts:
  16-Channel 12-bit PWM Servo Driver - I2C: You want to make a cool robot, maybe a hexapod walker, or maybe just a piece of art with a lot of moving parts. Or maybe you want to drive a lot of LEDs with precise PWM output. Using only two pins, control 16 free-running PWM outputs! You can even chain up 62 breakouts to control up to 992 PWM outputs.
  Battery: Your standard 2x 18650 battery pack (7,4 Volts)
